// Digital circuit Register 1 bit.dig as structural Verilog
module Register_1_bit (
  input  D,
  input  En,
  input  Clock,
  input  Clear,
  input  S,
  output Out
);

  wire multiplexer_1_out;

  Multiplexer multiplexer_1 (.sel(En), .in_0(Out), .in_1(D), .out(multiplexer_1_out));
  D_FF_AS d_ff_as_1 (.Set(S), .D(multiplexer_1_out), .C(Clock), .Clr(Clear), .Q(Out));  // open: nQ
endmodule
